// Logisim project S2-T20_FINAL.circ as structural Verilog: 4 circuits, main circuit main
module main (
  input  _0,
  input  _1,
  input  _2,
  input  _3,
  input  _4,
  input  _5,
  input  _6,
  input  _7,
  input  _8,
  input  _9,
  input  _10,
  input  in_12,
  input  _11,
  input  _12,
  input  _13,
  input  _14,
  input  _15,
  input  _0_2,
  input  _1_2,
  input  _2_2,
  input  _3_2,
  input  _4_2,
  input  _5_2,
  input  in_24,
  input  _6_2,
  input  in_26,
  input  _7_2,
  input  a3,
  input  b3,
  input  REVERSER,
  input  in_31,
  output out_32,
  output A3_2,
  output A2,
  output out_35,
  output out_36,
  output out_37,
  output a0,
  output out_39,
  output out_40,
  output out_41,
  output out_42,
  output B0,
  output B1,
  output B2,
  output B3_2,
  output out_47
);

  wire adder_1_cout, adder_2_cout, adder_3_cout, button_1_out, n0_4_counter_1_b0, n0_4_counter_1_b1,
       n0_4_counter_1_b2, n4_bit_comparator_1_a___b, n4_bit_comparator_1_a___b_2,
       n4_bit_comparator_1_a___b_3, n7_seg_circuit_1_a_2, n7_seg_circuit_1_b_2, n7_seg_circuit_1_c_2,
       n7_seg_circuit_1_d_2, n7_seg_circuit_1_e, n7_seg_circuit_1_f, n7_seg_circuit_1_g, or_1_out;

  Button button_1 (.out(button_1_out));
  Priority_Encoder #(.select(4)) priority_encoder_1 (
    .in0(_0), .in1(_1), .in2(_2), .in3(_3), .in4(_4), .in5(_5), .in6(_6), .in7(_7), .in8(_8), .in9(_9),
    .in10(_10), .in11(_11), .in12(_12), .in13(_13), .in14(_14), .in15(_15), .out({A3_2, A2, out_35, out_36}),
    .gs(out_37), .en_out(out_32), .en_in(in_12));
  Priority_Encoder priority_encoder_2 (
    .in0(_0_2), .in1(_1_2), .in2(_2_2), .in3(_3_2), .in4(_4_2), .in5(_5_2), .in6(_6_2), .in7(_7_2),
    .out({out_41, out_40, a0}), .en_in(in_26), .gs(out_42), .en_out(out_39));
  _0_4_COUNTER u_0_4_counter_1 (
    .REVERSER(REVERSER), .PUSH_BUTTON(button_1_out), .b2(n0_4_counter_1_b2), .b1(n0_4_counter_1_b1),
    .b0(n0_4_counter_1_b0));
  LED led_1 (.in(n0_4_counter_1_b2));
  LED led_2 (.in(n0_4_counter_1_b1));
  LED led_3 (.in(n0_4_counter_1_b0));
  _7_Segment_Display u_7_segment_display_1 (
    .g(n7_seg_circuit_1_g), .f(n7_seg_circuit_1_f), .a(n7_seg_circuit_1_a_2), .b(n7_seg_circuit_1_b_2),
    .e(n7_seg_circuit_1_e), .d(n7_seg_circuit_1_d_2), .c(n7_seg_circuit_1_c_2));  // open: dp
  Adder #(.width(1)) adder_1 (.a(a0), .b(n0_4_counter_1_b0), .out(B0), .cin(in_24), .cout(adder_1_cout));
  Adder #(.width(1)) adder_2 (.a(out_40), .b(n0_4_counter_1_b1), .out(B1), .cin(adder_1_cout), .cout(adder_2_cout));
  Adder #(.width(1)) adder_3 (.a(out_41), .b(n0_4_counter_1_b2), .out(B2), .cin(adder_2_cout), .cout(adder_3_cout));
  Adder #(.width(1)) adder_4 (.a(a3), .b(b3), .out(B3_2), .cin(adder_3_cout), .cout(out_47));
  _7__SEG_CIRCUIT u_7_seg_circuit_1 (
    .A(in_31), .B(n0_4_counter_1_b2), .C(n0_4_counter_1_b1), .D(n0_4_counter_1_b0),
    .a_2(n7_seg_circuit_1_a_2), .b_2(n7_seg_circuit_1_b_2), .c_2(n7_seg_circuit_1_c_2),
    .d_2(n7_seg_circuit_1_d_2), .e(n7_seg_circuit_1_e), .f(n7_seg_circuit_1_f), .g(n7_seg_circuit_1_g));
  _4_BIT_COMPARATOR u_4_bit_comparator_1 (
    .A0(out_36), .A1(out_35), .in_3(A2), .A3(A3_2), .in_5(B0), .in_6(B1), .in_7(B2), .in_8(B3_2),
    .A___B(n4_bit_comparator_1_a___b), .A___B_2(n4_bit_comparator_1_a___b_2),
    .A___B_3(n4_bit_comparator_1_a___b_3));
  or or_1 (or_1_out, n4_bit_comparator_1_a___b_2, n4_bit_comparator_1_a___b_3);
  LED led_4 (.in(n4_bit_comparator_1_a___b));
  LED led_5 (.in(or_1_out));

  // Notes on the sheet:
  //   TEAM - 20 (S2)
  //   CS254 :  SYED FARHAN
  //   CS265 :  YASHAS
  //   CS262 :  VISHRUTH S KUMAR
  //   OUTPUTS FROM
  //   MOISTURE SENSOR
  //   OUTPUTS FROM
  //   TEMPERATURE
  //   SENSOR
  //   CROP - SELECTOR
  //   PUSH - BUTTON
  //   4 - BIT PRIORITY ENCODER
  //   3 - BIT PRIORITY ENCODER
  //   0 - 4
  //   COUNTER CIRCUIT
  //   MOISTURE SENSING CUM WATERING SYSTEM
  //   A1
  //   A0
  //   a1
  //   a2
  //   b1
  //   b2
  //   b2
  //   b1
  //   HYRDO-SURE
  //   b0
  //   b0
  //   b2
  //   b0
  //   b1
  //   a0
  //   b0
  //   a1
  //   b1
  //   a2
  //   b2
  //   4 - BIT ADDER
  //   CROP NUMBER DISPLAY
  //   CIRCUIT
  //   7 - SEGMENT DISPLAY 
  //   1. Press the PUSH-BUTTON to 
  //   2. The display shows the crop type.
  //   than the desired threshold value.
  //   optimal for the growth of the crop.
  //   6. A3-A0 : outputs from moisture sensor
  //   B3-B0 : calculated threshold value
  //   a2 - a0 : outputs from temperature sensor
  //   b2 - b0 : outputs from crop selector circuit
  //   INSTRUCTIONS
  //   4. If the LED glows RED , it implies that the moisture value is less 
  //   3. The order of changing crops can be reversed by setting reverser to 1.
  //   5. If the LED glows GREEN , it implies that the desired moisture level is 
  //   A0
  //   A1
  //   A2
  //   A3
  //   B0
  //   B1
  //   B2
  //   B3
  //   select the crop type.
  //   4 - BIT COMPARATOR
  //   SAFE MOISTURE LEVEL
  //   UNSAFE MOISTURE LEVEL
  //   OUTPUT TO 
  //   DC MOTOR
endmodule

module _7__SEG_CIRCUIT (
  input  A,
  input  B,
  input  C,
  input  D,
  output a_2,
  output b_2,
  output c_2,
  output d_2,
  output e,
  output f,
  output g
);

  wire and_1_out, and_2_out, and_3_out, and_4_out, and_5_out, and_6_out, and_7_out, and_8_out, and_9_out,
       and_10_out, and_11_out, and_12_out, and_13_out, and_14_out, and_15_out, and_16_out, and_17_out,
       and_18_out, and_19_out, and_20_out, and_21_out, and_22_out, and_23_out, and_24_out, and_25_out,
       and_26_out, not_1_out, not_2_out, not_3_out, not_4_out, not_5_out, not_6_out, not_7_out, not_8_out,
       not_9_out, not_10_out, not_11_out, not_12_out, not_13_out, not_14_out, not_15_out, not_16_out,
       not_17_out, not_18_out, not_19_out, not_20_out, not_21_out, not_22_out, not_23_out, not_24_out,
       not_25_out, not_26_out, not_27_out, not_28_out, not_29_out, not_30_out, not_31_out, not_32_out,
       not_33_out, not_34_out, not_35_out, not_36_out, not_37_out, not_38_out, not_39_out, not_40_out,
       not_41_out, not_42_out, not_43_out, not_44_out, not_45_out, not_46_out, not_47_out, not_48_out,
       not_49_out, not_50_out, not_51_out, not_52_out;

  not not_1 (not_1_out, A);
  not not_2 (not_2_out, B);
  not not_3 (not_3_out, D);
  not not_4 (not_4_out, A);
  not not_5 (not_5_out, A);
  not not_6 (not_6_out, B);
  not not_7 (not_7_out, C);
  not not_8 (not_8_out, A);
  not not_9 (not_9_out, B);
  not not_10 (not_10_out, A);
  not not_11 (not_11_out, C);
  not not_12 (not_12_out, D);
  not not_13 (not_13_out, B);
  not not_14 (not_14_out, C);
  not not_15 (not_15_out, A);
  not not_16 (not_16_out, B);
  not not_17 (not_17_out, C);
  not not_18 (not_18_out, A);
  not not_19 (not_19_out, A);
  not not_20 (not_20_out, A);
  not not_21 (not_21_out, B);
  not not_22 (not_22_out, D);
  not not_23 (not_23_out, A);
  not not_24 (not_24_out, B);
  not not_25 (not_25_out, A);
  not not_26 (not_26_out, D);
  not not_27 (not_27_out, A);
  not not_28 (not_28_out, C);
  not not_29 (not_29_out, B);
  not not_30 (not_30_out, C);
  not not_31 (not_31_out, B);
  not not_32 (not_32_out, C);
  not not_33 (not_33_out, D);
  not not_34 (not_34_out, A);
  not not_35 (not_35_out, D);
  not not_36 (not_36_out, A);
  not not_37 (not_37_out, C);
  not not_38 (not_38_out, D);
  not not_39 (not_39_out, A);
  not not_40 (not_40_out, C);
  not not_41 (not_41_out, A);
  not not_42 (not_42_out, D);
  not not_43 (not_43_out, B);
  not not_44 (not_44_out, C);
  not not_45 (not_45_out, A);
  not not_46 (not_46_out, B);
  not not_47 (not_47_out, A);
  not not_48 (not_48_out, C);
  not not_49 (not_49_out, A);
  not not_50 (not_50_out, D);
  not not_51 (not_51_out, B);
  not not_52 (not_52_out, C);
  and and_1 (and_1_out, not_1_out, not_2_out, not_3_out);
  and and_2 (and_2_out, not_4_out, C);
  and and_3 (and_3_out, not_5_out, B, C);
  and and_4 (and_4_out, A, not_6_out, not_7_out);
  and and_5 (and_5_out, not_8_out, not_9_out);
  and and_6 (and_6_out, not_10_out, not_11_out, not_12_out);
  and and_7 (and_7_out, not_13_out, not_14_out);
  and and_8 (and_8_out, not_15_out, C, D);
  and and_9 (and_9_out, not_16_out, not_17_out);
  and and_10 (and_10_out, not_18_out, D);
  and and_11 (and_11_out, not_19_out, B);
  and and_12 (and_12_out, not_20_out, not_21_out, not_22_out);
  and and_13 (and_13_out, not_23_out, not_24_out, C);
  and and_14 (and_14_out, not_25_out, C, not_26_out);
  and and_15 (and_15_out, not_27_out, B, not_28_out, D);
  and and_16 (and_16_out, A, not_29_out, not_30_out);
  and and_17 (and_17_out, not_31_out, not_32_out, not_33_out);
  and and_18 (and_18_out, not_34_out, C, not_35_out);
  and and_19 (and_19_out, not_36_out, not_37_out, not_38_out);
  and and_20 (and_20_out, not_39_out, B, not_40_out);
  and and_21 (and_21_out, not_41_out, B, not_42_out);
  and and_22 (and_22_out, A, not_43_out, not_44_out);
  and and_23 (and_23_out, not_45_out, not_46_out, C);
  and and_24 (and_24_out, not_47_out, B, not_48_out);
  and and_25 (and_25_out, not_49_out, B, not_50_out);
  and and_26 (and_26_out, A, not_51_out, not_52_out);
  or or_1 (a_2, and_1_out, and_2_out, and_3_out, and_4_out);
  or or_2 (b_2, and_5_out, and_6_out, and_7_out, and_8_out);
  or or_3 (c_2, and_9_out, and_10_out, and_11_out);
  or or_4 (d_2, and_12_out, and_13_out, and_14_out, and_15_out, and_16_out);
  or or_5 (e, and_17_out, and_18_out);
  or or_6 (f, and_19_out, and_20_out, and_21_out, and_22_out);
  or or_7 (g, and_23_out, and_24_out, and_25_out, and_26_out);

  // Notes on the sheet:
  //   7 - SEGMENT DISPLAY CIRCUIT
endmodule

module _4_BIT_COMPARATOR (
  input  A0,
  input  A1,
  input  in_3,
  input  A3,
  input  in_5,
  input  in_6,
  input  in_7,
  input  in_8,
  output A___B,
  output A___B_2,
  output A___B_3
);

  wire and_1_out, and_2_out, and_3_out, and_4_out, and_6_out, and_7_out, and_8_out, and_9_out, not_1_out,
       not_2_out, not_3_out, not_4_out, not_5_out, not_6_out, not_7_out, not_8_out, xnor_1_out, xnor_2_out,
       xnor_3_out, xnor_4_out, xnor_5_out, xnor_6_out, xnor_7_out, xnor_8_out, xnor_9_out, xnor_10_out,
       xnor_11_out, xnor_12_out, xnor_13_out, xnor_14_out, xnor_15_out, xnor_16_out;

  xnor xnor_1 (xnor_1_out, A3, in_8);
  xnor xnor_2 (xnor_2_out, in_3, in_7);
  not not_1 (not_1_out, in_6);
  xnor xnor_3 (xnor_3_out, A3, in_8);
  xnor xnor_4 (xnor_4_out, in_3, in_7);
  xnor xnor_5 (xnor_5_out, A1, in_6);
  not not_2 (not_2_out, in_5);
  xnor xnor_6 (xnor_6_out, A3, in_8);
  xnor xnor_7 (xnor_7_out, in_3, in_7);
  xnor xnor_8 (xnor_8_out, A1, in_6);
  xnor xnor_9 (xnor_9_out, A0, in_5);
  xnor xnor_10 (xnor_10_out, A3, in_8);
  xnor xnor_11 (xnor_11_out, in_3, in_7);
  not not_3 (not_3_out, A1);
  xnor xnor_12 (xnor_12_out, A3, in_8);
  xnor xnor_13 (xnor_13_out, in_3, in_7);
  xnor xnor_14 (xnor_14_out, A1, in_6);
  not not_4 (not_4_out, A0);
  and and_1 (and_1_out, A3, not_5_out);
  not not_5 (not_5_out, in_8);
  xnor xnor_15 (xnor_15_out, A3, in_8);
  and and_2 (and_2_out, xnor_15_out, in_3, not_6_out);
  not not_6 (not_6_out, in_7);
  and and_3 (and_3_out, xnor_1_out, xnor_2_out, A1, not_1_out);
  and and_4 (and_4_out, xnor_3_out, xnor_4_out, xnor_5_out, A0, not_2_out);
  and and_5 (A___B_2, xnor_6_out, xnor_7_out, xnor_8_out, xnor_9_out);
  not not_7 (not_7_out, A3);
  and and_6 (and_6_out, not_7_out, in_8);
  xnor xnor_16 (xnor_16_out, A3, in_8);
  and and_7 (and_7_out, xnor_16_out, not_8_out, in_7);
  not not_8 (not_8_out, in_3);
  and and_8 (and_8_out, xnor_10_out, xnor_11_out, not_3_out, in_6);
  and and_9 (and_9_out, xnor_12_out, xnor_13_out, xnor_14_out, not_4_out, in_5);
  or or_1 (A___B, and_1_out, and_2_out, and_3_out, and_4_out);
  or or_2 (A___B_3, and_6_out, and_7_out, and_8_out, and_9_out);

  // Notes on the sheet:
  //   A2
  //   B0
  //   B1
  //   B2
  //   B3
  //   4 - BIT COMPARATOR
endmodule

module _0_4_COUNTER (
  input  REVERSER,
  input  PUSH_BUTTON,
  output b2,
  output b1,
  output b0
);

  wire and_1_out, and_2_out, and_3_out, and_4_out, and_5_out, and_6_out, and_7_out, not_1_out, or_1_out,
       or_2_out, or_3_out, or_4_out, or_5_out, t_ff_1_qn, t_ff_2_qn, t_ff_3_qn;

  not not_1 (not_1_out, REVERSER);
  T_Flip_Flop t_ff_1 (.clk(PUSH_BUTTON), .T(or_4_out), .Q(b2), .Qn(t_ff_1_qn));  // open: preset, reset, en
  and and_1 (and_1_out, and_6_out, b0);
  and and_2 (and_2_out, not_1_out, t_ff_1_qn, b1, b0);
  and and_3 (and_3_out, t_ff_1_qn, b1, REVERSER, t_ff_3_qn);
  or or_1 (or_1_out, and_3_out, and_1_out, and_4_out);
  T_Flip_Flop t_ff_2 (.clk(PUSH_BUTTON), .T(or_1_out), .Q(b1), .Qn(t_ff_2_qn));  // open: preset, reset, en
  or or_2 (or_2_out, REVERSER, b2);
  or or_3 (or_3_out, and_4_out, and_6_out, and_7_out);
  or or_4 (or_4_out, and_5_out, and_2_out);
  and and_4 (and_4_out, b2, t_ff_3_qn, REVERSER, t_ff_2_qn);
  and and_5 (and_5_out, t_ff_2_qn, or_2_out, t_ff_3_qn);
  T_Flip_Flop t_ff_3 (.clk(PUSH_BUTTON), .T(or_3_out), .Q(b0), .Qn(t_ff_3_qn));  // open: preset, reset, en
  and and_6 (and_6_out, not_1_out, t_ff_1_qn);
  and and_7 (and_7_out, REVERSER, or_5_out, t_ff_1_qn);
  or or_5 (or_5_out, b0, b1);

  // Notes on the sheet:
  //   0 - 4 COUNTER CIRCUIT
endmodule
